# Fritzing sketch ds-touch-backpack-with-edison-arduino (saved by Fritzing 0.9.1b)

parts:
  Part1 = Arduino Pro Mini v13
  SparkFun1 = DS Touch
  Part2 = Intel Edison Arduinobreakout

nets:
  N1: Part1.A4, Part2.A4/SDA
  N2: Part1.A5, Part2.A5/SCL
  GND: Part1.GND, Part2.GND
  VCC: Part1.VCC, Part2.5V
  N3: Part1.A3, SparkFun1.X1
  N4: Part1.A2, SparkFun1.Y2
  N5: Part1.A1, SparkFun1.X2
  N6: Part1.A0, SparkFun1.Y1

custom parts:
  DS Touch: Nintendo DS Touch screen
