# Fritzing sketch ds-touch-backpack-with-edison-mini (saved by Fritzing 0.9.1b)

parts:
  Part1 = Arduino Pro Mini v13
  SparkFun1 = DS Touch
  U1 = EDISON

nets:
  N1: Part1.A4, U1.GP20
  N2: Part1.A5, U1.GP27
  GND: Part1.GND, U1.GND
  N3: Part1.VCC, U1.V_V3P30
  N4: Part1.A3, SparkFun1.X1
  N5: Part1.A2, SparkFun1.Y2
  N6: Part1.A1, SparkFun1.X2
  N7: Part1.A0, SparkFun1.Y1

custom parts:
  DS Touch: Nintendo DS Touch screen
