# Fritzing sketch ds-touch-backpack-with-tessel-2 (saved by Fritzing 0.9.1b)

parts:
  Part1 = Arduino Pro Mini v13
  SparkFun1 = DS Touch
  Part2 = Tessel 2

nets:
  N1: Part1.A4, Part2.1
  N2: Part1.A5, Part2.0
  GND: Part1.GND, Part2.GND
  VCC: Part1.VCC, Part2.3V3
  N3: Part1.A3, SparkFun1.X1
  N4: Part1.A2, SparkFun1.Y2
  N5: Part1.A1, SparkFun1.X2
  N6: Part1.A0, SparkFun1.Y1

custom parts:
  DS Touch: Nintendo DS Touch screen
  Tessel 2: Draft version of Tessel 2
