# Fritzing sketch ds-touch-backpack (saved by Fritzing 0.9.1b)

parts:
  Part1 = Arduino Pro Mini v13
  SparkFun1 = DS Touch

nets:
  N1: Part1.A3, SparkFun1.X1
  N2: Part1.A2, SparkFun1.Y2
  N3: Part1.A1, SparkFun1.X2
  N4: Part1.A0, SparkFun1.Y1

notes:
  SDA
  SCL
  5V
  GND
  Upload ds_touch_slave.ino to the Pro Mini

custom parts:
  DS Touch: Nintendo DS Touch screen
