# Fritzing sketch wiring (saved by Fritzing 0.9.1b)

parts:
  Part1 = Arduino Uno (Rev3) - ICSP
  Part2 = Arduino Uno (Rev3) - ICSP

nets:
  N1: Part1.A4/SDA, Part2.A4/SDA
  N2: Part1.A5/SCL, Part2.A5/SCL
  5V: Part1.5V, Part2.5V
  GND: Part1.GND, Part2.GND

notes:
  y1 x2 y2 x1
  ds_touch_slave.ino
  StandardFirmata
